# Fritzing sketch tempBarGauge (saved by Fritzing 0.9.3b)

parts:
  Part2 = Adafruit Pro Trinket 3.3V 12MHz [part_number="Adafruit #2010"]
  Part3 = Adafruit MAX31856 Thermocouple Amp [part_number="Adafruit #3263"]
  U1 = POT [package=pot_alpha_rv16af-20]
  U2 = POT [package=pot_mammoth]
  Part4 = Bi-Color 24-Bar Bargraph w I2C Backpack [part_number=1721]
  Part5 = Bi-Color 24-Bar Bargraph w I2C Backpack [part_number=1721]

nets:
  GND: Part2.GND, Part3.GND, U1.A, U2.S, Part4.GND, Part5.GND
  VDD: Part2.+3V3, Part3.VIN, U1.E, U2.E, Part4.VDD, Part5.VDD
  N1: Part2.D10, Part3.!CS
  N2: Part2.D11, Part3.SDI
  N3: Part2.D12, Part3.SDO
  N4: Part2.D13, Part3.SCK
  N5: Part2.A0, U1.S
  N6: Part2.A1, U2.A
  N7: Part2.A4, Part4.SDA, Part5.SDA
  N8: Part2.A5, Part4.SCL, Part5.SCL

notes:
  Scale Pot.
  Shift Pot.
  Thermocouple (polarity is important)
  bar graphs should have different addresses. simply solder jumper marked A0 on the back side of the second bar graph

custom parts:
  Adafruit Pro Trinket 3.3V 12MHz: rinket's got a big sister in town - the Pro Trinket 3V! Pro Trinket combines everything you love about Trinket with the familiarity of the core Arduino chip, the ATmega328. It's like an Arduino Pro Mini with more pins and USB tossed in. Trinket's a year old now, and while its been great to see tons of tiny projects, sometimes you just need more pins, more FLASH, and more RAM. That's why we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
  Adafruit MAX31856 Thermocouple Amp: Thermocouples are very sensitive, requiring a good amplifier with a cold-compensation reference, as well as calculations to handle any non-linearities. For a long time we've suggested our MAX31855K breakout, which works great but is only for K-type thermocouples. Now we're happy to offer a great new thermocouple amplifier/converter that can handle just about any type of thermocouple, and even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
  Bi-Color 24-Bar Bargraph w I2C Backpack: What's better than a single LED? Lots of LEDs! A fun way to make a small linear display is to use two 12-bar Bi-color bar-graphs. Much like our 8x8 and 7-segment backpacks, this backpack pairs perfectly with our bar-graphs and manages all the LED control and multiplexing.
